# Fritzing sketch Clock_Messenger (saved by Fritzing 0.9.3b)
breadboards: 1

parts:
  WeMos_D1_Mini1 = WeMos D1 Mini  # not connected
  J1 = Piezo Speaker
  Componente1 = Display LED de 8 dígitos basado en MAX7219  # not connected
  M1 = MAX7219 8x8 single Led Matrix Module
  Q1 = NPN-Transistor [package="TO92 [THT]"]
  R1 = Resistor [tolerance=±5% resistance=220 package=THT]
  D1 = Rectifier Diode [part_number=1N4001 package="300 mil [THT]"]

nets:
  N1: J1.pin1, Q1.C, D1.anode
  N2: J1.pin2, M1.I-CLK-3, M1.I-CS-3, M1.O-VCC-3, M1.O-GND-3, M1.O-DOUT-3, M1.O-CS-3, M1.O-CLK-3, D1.cathode
  N3: M1.I-CLK-4, M1.I-CS-4, M1.I-DIN-4, M1.I-GND-4, M1.I-VCC-4, M1.O-VCC-4, M1.O-GND-4, M1.O-CS-4, M1.O-CLK-4, Q1.E
  N4: Q1.B, R1.Pin_0

custom parts:
  MAX7219 8x8 single Led Matrix Module: Description: MAX7219 8x8 LedMatrix single Red Module Dimensions: 32x32mm Documents:
